// Logisim project harvard-risc-16bit.circ as structural Verilog: 3 circuits, main circuit main
module main (
  input  [15:0] in_1
);

  wire A, A_EN, and_1_out, and_2_out, and_3_out, and_4_out, BAD_OP, CLK, clock_1_out, comparator_1_gt,
       comparator_1_lt, F2, HALT, I_O_EN, IDX__EN, LINK_EN, nor_1_out, not_1_out, not_2_out, not_3_out,
       or_1_out, PC_EN, RAM_EN, RESET_out, ROM__EN, t_ff_1_q, t_ff_1_qn, t_ff_2_q, t_ff_2_qn;
  wire [3:0] ALU_OP, SHIFT;
  wire [7:0] OPCODE;
  wire [11:0] CTRL_WORD;
  wire [15:0] ACC, adder_1_out, alu_1_alu_out, controlled_buffer_1_out, counter_1_q, multiplexer_1_out,
       register_1_q, register_2_q, register_3_q;
  wire [15:4] rom_1_data;

  Clock clock_1 (.out(clock_1_out));
  // Probe on register_1_q
  Comparator #(.width(16)) comparator_1 (
    .a(ACC), .b({16{1'b0}}), .gt(comparator_1_gt), .lt(comparator_1_lt));  // open: eq
  Button RESET (.out(RESET_out));
  LED led_1 (.in(BAD_OP));
  Register #(.width(16), .Select("low")) register_1 (
    .D(controlled_buffer_1_out), .en(CTRL_WORD[6]), .Q(register_1_q), .clk(CLK));  // open: clr
  assign controlled_buffer_1_out = I_O_EN ? in_1 : 16'bz;  // Controlled_Buffer controlled_buffer_1
  and and_1 (and_1_out, CTRL_WORD[3], or_1_out);
  nor nor_1 (nor_1_out, CTRL_WORD[8], CTRL_WORD[7]);
  and and_2 (and_2_out, CTRL_WORD[8], comparator_1_lt);
  and and_3 (and_3_out, CTRL_WORD[7], comparator_1_gt);
  and and_4 (and_4_out, clock_1_out, ~HALT, ~BAD_OP);  // AND_Gate
  not not_1 (not_1_out, and_1_out);
  or or_1 (or_1_out, nor_1_out, and_2_out, and_3_out);
  not not_2 (not_2_out, and_4_out);
  and and_5 (HALT, OPCODE[0], OPCODE[1], OPCODE[2], OPCODE[3], OPCODE[4], OPCODE[5], OPCODE[6], OPCODE[7]);
  Counter #(.width(16), .max('hffff), .behavior("old")) counter_1 (
    .load(and_1_out), .D(controlled_buffer_1_out), .count(not_1_out), .Q(counter_1_q), .clk(F2),
    .clr(RESET_out));  // open: carry, preset
  T_Flip_Flop #(.Pre_Clr_Positions("LEGACY"), .enable("true"), .NewFFLayout("false")) t_ff_1 (
    .clk(not_2_out), .T(1'b1), .Q(t_ff_1_q), .Qn(t_ff_1_qn), .reset(RESET_out));  // open: preset, en
  T_Flip_Flop #(.Pre_Clr_Positions("LEGACY"), .enable("true"), .NewFFLayout("false")) t_ff_2 (
    .clk(and_4_out), .T(1'b1), .Q(t_ff_2_q), .Qn(t_ff_2_qn), .reset(RESET_out));  // open: preset, en
  assign controlled_buffer_1_out = PC_EN ? counter_1_q : 16'bz;  // Controlled_Buffer controlled_buffer_2
  Adder #(.width(16)) adder_1 (.a(16'h1), .b(counter_1_q), .out(adder_1_out));  // open: cin, cout
  and and_6 (CLK, and_4_out, t_ff_1_qn, t_ff_2_q);
  and and_7 (F2, t_ff_2_qn, t_ff_1_q, and_4_out);
  Register #(.width(16), .Select("low")) register_2 (
    .D(adder_1_out), .en(CTRL_WORD[4]), .Q(register_2_q), .clk(CLK));  // open: clr
  ROM #(.addrWidth(16), .dataWidth(24), .Select("high")) rom_1 (.addr(counter_1_q), .data({OPCODE, rom_1_data, SHIFT}));
  assign controlled_buffer_1_out = LINK_EN ? register_2_q : 16'bz;  // Controlled_Buffer controlled_buffer_3
  // Probe on {rom_1_data, SHIFT}
  Decoder #(.select(3), .disabled(0), .enable("false")) decoder_1 (
    .out0(A_EN), .out1(RAM_EN), .out2(PC_EN), .out3(ROM__EN), .out4(LINK_EN), .out5(I_O_EN), .out6(IDX__EN),
    .sel(CTRL_WORD[11:9]));  // open: out7
  nor nor_2 (BAD_OP, CTRL_WORD[0], A, CTRL_WORD[2], CTRL_WORD[3], CTRL_WORD[4], CTRL_WORD[5], CTRL_WORD[6], CTRL_WORD[7], CTRL_WORD[8], CTRL_WORD[9], CTRL_WORD[10], CTRL_WORD[11], ALU_OP[0], ALU_OP[1], ALU_OP[2], ALU_OP[3]);
  assign controlled_buffer_1_out = ROM__EN ? {rom_1_data, SHIFT} : 16'bz;  // Controlled_Buffer controlled_buffer_4
  Register #(.width(16), .Select("low")) register_3 (
    .D(controlled_buffer_1_out), .en(CTRL_WORD[0]), .Q(register_3_q), .clk(CLK));  // open: clr
  Multiplexer #(.width(16), .disabled(0), .enable("false")) multiplexer_1 (
    .in0(register_3_q), .in1({rom_1_data, SHIFT}), .out(multiplexer_1_out), .sel(not_3_out));
  not not_3 (not_3_out, CTRL_WORD[5]);
  assign controlled_buffer_1_out = IDX__EN ? register_3_q : 16'bz;  // Controlled_Buffer controlled_buffer_5
  // Probe on multiplexer_1_out
  RAM #(.addrWidth(16), .dataWidth(16), .Select("high"), .simpleMode("false")) ram_1 (
    .addr(multiplexer_1_out), .data(controlled_buffer_1_out), .sel(CTRL_WORD[2]), .clk(CLK), .ld(RAM_EN));  // open: clr
  ROM #(.dataWidth(16), .Select("high")) rom_2 (.addr(OPCODE), .data({ALU_OP, CTRL_WORD[11:2], A, CTRL_WORD[0]}));
  ALU alu_1 (.B(controlled_buffer_1_out), .A(ACC), .SHIFT(SHIFT), .ALU_OP(ALU_OP), .ALU_OUT(alu_1_alu_out));
  assign controlled_buffer_1_out = A_EN ? ACC : 16'bz;  // Controlled_Buffer controlled_buffer_6
  Register #(.width(16), .Select("low")) register_4 (.D(alu_1_alu_out), .en(A), .Q(ACC), .clk(CLK));  // open: clr

  // Other names for the same wires on the sheet: IDX = CTRL_WORD[0]; CTRL_WORD (some bits) = {ALU_OP, A};
  //   RAM = CTRL_WORD[2]; PC = CTRL_WORD[3]; LINK = CTRL_WORD[4]; INDIR = CTRL_WORD[5]; I_O = CTRL_WORD[6];
  //   JPOS = CTRL_WORD[7]; JNEG = CTRL_WORD[8]; SRC[2:0] = CTRL_WORD[11:9]; F1 = CLK

  // Notes on the sheet:
  //   Designed by S. Gražulis (https://saulius.grazulis.lt) CC-BY-NC
  //   PC
  //   Program ROM
  //   LINK
  //   contents of rom_1 (hex, n*v repeats v):
  //   20001 40000 40001 20000 40002 30001 b0000 60000 40001 c0000 40000 30002 190001 40002 1a000a a0005
  //   ffffff
  //   Decode data source
  //   IDX
  //   Data RAM
  //   Decoder ROM
  //   contents of rom_2 (hex, n*v repeats v):
  //   e00 8226 8602 8206 4 8a02 40 608 788 688 708 206 1206 2206 3206 4206 5206 6206 7206 9206 a206 b206
  //   c206 d206 e206 602 1602 2602 3602 4602 c602 d602 e602 226 1226 2226 3226 4226 c226 d226 e226 601 205
  //   1 8c02 fc02 24 c02 1c02 206*0 1
  //   Acc
endmodule

module ALU (
  input  [15:0] B,
  input  [15:0] A,
  input  [3:0] SHIFT,
  input  [3:0] ALU_OP,
  output [15:0] ALU_OUT
);

  wire [15:0] adder_1_out, adder_2_out, adder_3_out, and_1_out, divider_1_out, divider_1_rem,
       multiplier_1_out, negator_1_out, or_1_out, shifter_1_out, shifter_2_out, shifter_3_out, shifter_4_out,
       shifter_5_out, subtractor_1_out, xor_1_out;

  Adder #(.width(16)) adder_1 (.a(A), .b(B), .out(adder_1_out));  // open: cin, cout
  Subtractor #(.width(16)) subtractor_1 (.a(A), .b(B), .out(subtractor_1_out));  // open: bin, bout
  Multiplier #(.width(16)) multiplier_1 (.a(A), .b(B), .out(multiplier_1_out));  // open: cin, cout
  Divider #(.width(16)) divider_1 (.a(A), .b(B), .out(divider_1_out), .rem(divider_1_rem));  // open: upper
  Shifter #(.width(16)) shifter_1 (.in(A), .\dist (SHIFT), .out(shifter_1_out));
  Shifter #(.width(16), .shift("lr")) shifter_2 (.in(A), .\dist (SHIFT), .out(shifter_2_out));
  Negator #(.width(16)) negator_1 (.in(A), .out(negator_1_out));
  Adder #(.width(16)) adder_2 (.a(B), .b({16{1'b0}}), .out(adder_2_out));  // open: cin, cout
  Shifter #(.width(16), .shift("rl")) shifter_3 (.in(A), .\dist (SHIFT), .out(shifter_3_out));
  Shifter #(.width(16), .shift("rr")) shifter_4 (.in(A), .\dist (SHIFT), .out(shifter_4_out));
  Shifter #(.width(16), .shift("ar")) shifter_5 (.in(A), .\dist (SHIFT), .out(shifter_5_out));
  assign and_1_out = A & B;  // AND_Gate and_1, 16 bits wide
  assign or_1_out = A | B;  // OR_Gate or_1, 16 bits wide
  assign xor_1_out = A ^ B;  // XOR_Gate xor_1, 16 bits wide
  Adder #(.width(16)) adder_3 (.a(B), .b(16'h1), .out(adder_3_out));  // open: cin, cout
  Multiplexer #(.select(4), .width(16), .disabled(0), .enable("false")) multiplexer_1 (
    .in0(adder_1_out), .in1(subtractor_1_out), .in2(multiplier_1_out), .in3(divider_1_out),
    .in4(divider_1_rem), .in5(shifter_1_out), .in6(shifter_2_out), .in7(negator_1_out), .in8(adder_2_out),
    .in9(shifter_3_out), .in10(shifter_4_out), .in11(shifter_5_out), .in12(and_1_out), .in13(or_1_out),
    .in14(xor_1_out), .in15(adder_3_out), .out(ALU_OUT), .sel(ALU_OP));
endmodule

module other (
);

  wire CLK;
  wire [15:0] counter_1_q;
  wire [23:0] Program_ROM_data;

  Clock clock_1 (.out(CLK));
  Counter #(.width(16), .max('hffff)) counter_1 (
    .Q(counter_1_q), .clk(CLK));  // open: load, D, count, carry, clr, preset, down
  ROM #(.addrWidth(16), .dataWidth(24), .Select("low")) Program_ROM (.addr(counter_1_q), .data(Program_ROM_data));
endmodule
