// Logisim project conditional-jump-logic.circ as structural Verilog: 1 circuit, main circuit main
module main (
  input  JPOS,
  input  JNEG,
  input  GT0,
  input  LT0,
  output JMP
);

  wire and_1_out, and_2_out, and_3_out, not_1_out, not_2_out;

  not not_1 (not_1_out, JPOS);
  and and_1 (and_1_out, not_1_out, not_2_out);
  not not_2 (not_2_out, JNEG);
  and and_2 (and_2_out, JNEG, LT0);
  and and_3 (and_3_out, JPOS, GT0);
  or or_1 (JMP, and_1_out, and_2_out, and_3_out);

  // Notes on the sheet:
  //   Designed by S. Gražulis (https://saulius.grazulis.lt) CC-BY-NC
endmodule
