// Logisim project stack.circ as structural Verilog: 4 circuits, main circuit 16bit-stack2
module _16bit_stack2 (
  input  [15:0] DATA_IN,
  input  [15:0] CARRY_IN,
  input  PUSH,
  input  POP,
  input  SWAP,
  input  SEL,
  input  CLOCK,
  output [15:0] TOP,
  output [15:0] NEXT,
  output [15:0] LAST,
  output [15:0] CARRY_OUT
);

  wire and_2_out, and_3_out, and_4_out, BAD_OP, CLOCK_t, controlled_buffer_1_out, MODE, not_1_out, not_3_out,
       or_1_out;
  wire [15:0] controlled_buffer_4_out, controlled_buffer_6_out, controlled_buffer_7_out;

  or or_1 (or_1_out, SWAP, POP, PUSH);
  and and_1 (CLOCK_t, or_1_out, not_1_out, CLOCK);
  not not_1 (not_1_out, BAD_OP);
  and and_2 (and_2_out, PUSH, POP);
  and and_3 (and_3_out, PUSH, SWAP);
  and and_4 (and_4_out, POP, SWAP);
  assign controlled_buffer_1_out = POP ? PUSH : 1'bz;  // Controlled_Buffer controlled_buffer_1
  not not_2 (controlled_buffer_1_out, POP);
  or or_2 (BAD_OP, and_2_out, and_3_out, and_4_out);
  assign MODE = not_3_out ? controlled_buffer_1_out : 1'bz;  // Controlled_Buffer controlled_buffer_2
  not not_3 (not_3_out, SWAP);
  assign MODE = SWAP ? 1'b0 : 1'bz;  // Controlled_Buffer controlled_buffer_3
  Register #(.width(16), .Select("low")) register_1 (
    .D(controlled_buffer_4_out), .Q(TOP), .clk(CLOCK_t), .cs(SEL));  // open: en, clr, preset
  assign controlled_buffer_4_out = MODE ? DATA_IN : 16'bz;  // Controlled_Buffer controlled_buffer_4
  assign controlled_buffer_4_out = ~MODE ? LAST : 16'bz;  // Controlled_Buffer controlled_buffer_5
  assign controlled_buffer_6_out = MODE ? TOP : 16'bz;  // Controlled_Buffer controlled_buffer_6
  assign CARRY_OUT = TOP;  // Buffer buffer_1, 16 bits wide
  assign controlled_buffer_7_out = SWAP ? TOP : 16'bz;  // Controlled_Buffer controlled_buffer_7
  Register #(.width(16), .Select("low")) register_2 (
    .D(controlled_buffer_6_out), .Q(LAST), .clk(CLOCK_t), .cs(SEL));  // open: en, clr, preset
  assign controlled_buffer_6_out = ~MODE ? controlled_buffer_7_out : 16'bz;  // Controlled_Buffer controlled_buffer_8
  assign controlled_buffer_7_out = ~SWAP ? CARRY_IN : 16'bz;  // Controlled_Buffer controlled_buffer_9

  assign NEXT = LAST;

  // Other names for the same wires on the sheet: POP_OP = POP; PUSH_OP = PUSH; SWAP_OP = SWAP
endmodule

module _16bit_stack8 (
  input  [15:0] DATA_IN,
  input  [15:0] CARRY_IN,
  input  PUSH,
  input  POP,
  input  SEL,
  input  CLOCK,
  input  SWAP,
  output [15:0] TOP,
  output [15:0] NEXT,
  output [15:0] LAST,
  output [15:0] CARRY_OUT
);

  wire [15:0] n16bit_stack2_1_last, n16bit_stack2_2_carry_out, n16bit_stack2_2_last,
       n16bit_stack2_3_carry_out, n16bit_stack2_3_last, n16bit_stack2_4_carry_out;

  _16bit_stack2 u_16bit_stack2_1 (
    .DATA_IN(DATA_IN), .CARRY_OUT(CARRY_OUT), .PUSH(PUSH), .POP(POP), .SWAP(SWAP), .TOP(TOP), .NEXT(NEXT),
    .SEL(SEL), .CLOCK(CLOCK), .LAST(n16bit_stack2_1_last), .CARRY_IN(n16bit_stack2_2_carry_out));
  _16bit_stack2 u_16bit_stack2_2 (
    .DATA_IN(n16bit_stack2_1_last), .CARRY_OUT(n16bit_stack2_2_carry_out), .PUSH(PUSH), .POP(POP),
    .SWAP(1'b0), .SEL(SEL), .CLOCK(CLOCK), .LAST(n16bit_stack2_2_last), .CARRY_IN(n16bit_stack2_3_carry_out));  // open: TOP, NEXT
  _16bit_stack2 u_16bit_stack2_3 (
    .DATA_IN(n16bit_stack2_2_last), .CARRY_OUT(n16bit_stack2_3_carry_out), .PUSH(PUSH), .POP(POP),
    .SWAP(1'b0), .SEL(SEL), .CLOCK(CLOCK), .LAST(n16bit_stack2_3_last), .CARRY_IN(n16bit_stack2_4_carry_out));  // open: TOP, NEXT
  _16bit_stack2 u_16bit_stack2_4 (
    .DATA_IN(n16bit_stack2_3_last), .CARRY_OUT(n16bit_stack2_4_carry_out), .PUSH(PUSH), .POP(POP),
    .SWAP(1'b0), .SEL(SEL), .CLOCK(CLOCK), .LAST(LAST), .CARRY_IN(CARRY_IN));  // open: TOP, NEXT

  // Other names for the same wires on the sheet: POP_OP = POP; PUSH_OP = PUSH; SWAP_OP = SWAP

  // Notes on the sheet:
  //   16bit-stack8
endmodule

module _16bit_stack32 (
  input  [15:0] DATA_IN,
  input  [15:0] CARRY_IN,
  input  PUSH,
  input  POP,
  input  SEL,
  input  CLOCK,
  input  SWAP,
  output [15:0] TOP,
  output [15:0] NEXT,
  output [15:0] LAST,
  output [15:0] CARRY_OUT
);

  wire [15:0] n16bit_stack8_1_last, n16bit_stack8_2_carry_out, n16bit_stack8_2_last,
       n16bit_stack8_3_carry_out, n16bit_stack8_3_last, n16bit_stack8_4_carry_out;

  _16bit_stack8 u_16bit_stack8_1 (
    .DATA_IN(DATA_IN), .CARRY_OUT(CARRY_OUT), .PUSH(PUSH), .POP(POP), .SWAP(SWAP), .TOP(TOP), .NEXT(NEXT),
    .SEL(SEL), .CLOCK(CLOCK), .LAST(n16bit_stack8_1_last), .CARRY_IN(n16bit_stack8_2_carry_out));
  _16bit_stack8 u_16bit_stack8_2 (
    .DATA_IN(n16bit_stack8_1_last), .CARRY_OUT(n16bit_stack8_2_carry_out), .PUSH(PUSH), .POP(POP),
    .SWAP(1'b0), .SEL(SEL), .CLOCK(CLOCK), .LAST(n16bit_stack8_2_last), .CARRY_IN(n16bit_stack8_3_carry_out));  // open: TOP, NEXT
  _16bit_stack8 u_16bit_stack8_3 (
    .DATA_IN(n16bit_stack8_2_last), .CARRY_OUT(n16bit_stack8_3_carry_out), .PUSH(PUSH), .POP(POP),
    .SWAP(1'b0), .SEL(SEL), .CLOCK(CLOCK), .LAST(n16bit_stack8_3_last), .CARRY_IN(n16bit_stack8_4_carry_out));  // open: TOP, NEXT
  _16bit_stack8 u_16bit_stack8_4 (
    .DATA_IN(n16bit_stack8_3_last), .CARRY_OUT(n16bit_stack8_4_carry_out), .PUSH(PUSH), .POP(POP),
    .SWAP(1'b0), .SEL(SEL), .CLOCK(CLOCK), .LAST(LAST), .CARRY_IN(CARRY_IN));  // open: TOP, NEXT

  // Other names for the same wires on the sheet: POP_OP = POP; PUSH_OP = PUSH; SWAP_OP = SWAP

  // Notes on the sheet:
  //   16bit-stack32
endmodule

module _16bit_stack128 (
  input  [15:0] DATA_IN,
  input  [15:0] CARRY_IN,
  input  PUSH,
  input  POP,
  input  SEL,
  input  CLOCK,
  input  SWAP,
  output [15:0] TOP,
  output [15:0] NEXT,
  output [15:0] LAST,
  output [15:0] CARRY_OUT
);

  wire [15:0] n16bit_stack32_1_last, n16bit_stack32_2_carry_out, n16bit_stack32_2_last,
       n16bit_stack32_3_carry_out, n16bit_stack32_3_last, n16bit_stack32_4_carry_out;

  _16bit_stack32 u_16bit_stack32_1 (
    .DATA_IN(DATA_IN), .CARRY_OUT(CARRY_OUT), .PUSH(PUSH), .POP(POP), .SWAP(SWAP), .TOP(TOP), .NEXT(NEXT),
    .SEL(SEL), .CLOCK(CLOCK), .LAST(n16bit_stack32_1_last), .CARRY_IN(n16bit_stack32_2_carry_out));
  _16bit_stack32 u_16bit_stack32_2 (
    .DATA_IN(n16bit_stack32_1_last), .CARRY_OUT(n16bit_stack32_2_carry_out), .PUSH(PUSH), .POP(POP),
    .SWAP(1'b0), .SEL(SEL), .CLOCK(CLOCK), .LAST(n16bit_stack32_2_last), .CARRY_IN(n16bit_stack32_3_carry_out));  // open: TOP, NEXT
  _16bit_stack32 u_16bit_stack32_3 (
    .DATA_IN(n16bit_stack32_2_last), .CARRY_OUT(n16bit_stack32_3_carry_out), .PUSH(PUSH), .POP(POP),
    .SWAP(1'b0), .SEL(SEL), .CLOCK(CLOCK), .LAST(n16bit_stack32_3_last), .CARRY_IN(n16bit_stack32_4_carry_out));  // open: TOP, NEXT
  _16bit_stack32 u_16bit_stack32_4 (
    .DATA_IN(n16bit_stack32_3_last), .CARRY_OUT(n16bit_stack32_4_carry_out), .PUSH(PUSH), .POP(POP),
    .SWAP(1'b0), .SEL(SEL), .CLOCK(CLOCK), .LAST(LAST), .CARRY_IN(CARRY_IN));  // open: TOP, NEXT

  // Other names for the same wires on the sheet: POP_OP = POP; PUSH_OP = PUSH; SWAP_OP = SWAP

  // Notes on the sheet:
  //   16bit-stack128
endmodule
